# Fritzing sketch diagram (saved by Fritzing 0.9.6b)
breadboards: 2

parts:
  Part1 = Arduino Nano (Rev3.0)
  Combo-Sensor = Adafruit BME680
  R1 = 8 Resistor Network [part_number=10kΩ package="SIP (Single Inline)"]
  R2 = Resistor [tolerance=±5% resistance=100 package="2512 [SMD]"]
  R3 = Resistor [tolerance=±5% resistance=220 package="2512 [SMD]"]
  R4 = Resistor [tolerance=±5% resistance=220 package="2512 [SMD]"]
  DIP = DIP Switch 8 Position [package=dipswitch-08]
  LED = RGB LED (com. cathode, rbg) [package="5 mm [THT]"]
  R5 = Resistor [tolerance=±5% resistance=2.2k package="2512 [SMD]"]
  Soil_Hygrometer = DFRobot Capacitive Soil Moisture Sensor V1.0 [part_number=SEN0193]
  Phototransistor = LTR-301 [package=ltr-301]
  S1 = Momentary Switch [package=ksa_sealed_tac_switch]
  S2 = Momentary Switch [package=ksa_sealed_tac_switch]
  S3 = Momentary Switch [package=ksa_sealed_tac_switch]
  R6/R7/R8 = Resistor [tolerance=±5% resistance=10k package="2512 [SMD]"]
  R7 = Resistor [tolerance=±5% resistance=10k package="2512 [SMD]"]
  R8 = Resistor [tolerance=±5% resistance=10k package="2512 [SMD]"]
  Buzzer = Piezo Speaker

nets:
  GND: Part1.GND, Combo-Sensor.GND, R1.1, LED.common_cathode, R5.Pin_0, Soil_Hygrometer.GND, R6/R7/R8.Pin_0, R7.Pin_0, R8.Pin_0, Buzzer.pin1
  N1: Part1.D2, S3.2, R6/R7/R8.Pin_1
  N2: Part1.D3, S2.2, R8.Pin_1
  N3: Part1.D4, S1.2, R7.Pin_1
  N4: Part1.D5, R1.2, DIP.8
  N5: Part1.D6, R1.3, DIP.7
  N6: Part1.D7, R1.4, DIP.6
  N7: Part1.D8, R1.5, DIP.5
  N8: Part1.D9, R1.6, DIP.4
  N9: Part1.D10, R1.7, DIP.3
  N10: Part1.D11/MOSI, R1.8, DIP.2
  N11: Part1.D12/MISO, R1.9, DIP.1
  N12: Part1.A7, R5.Pin_1, Phototransistor.E
  N13: Part1.A6, Soil_Hygrometer.A
  N14: Part1.A5, Combo-Sensor.SCK/SCL
  N15: Part1.A4, Combo-Sensor.SDO/ADR, Combo-Sensor.SDI/SDA
  N16: Part1.A3, Buzzer.pin2
  N17: Part1.A2, R3.Pin_0
  N18: Part1.A1, R4.Pin_0
  N19: Part1.A0, R2.Pin_0
  3V3: Part1.3V3, Combo-Sensor.VIN, Combo-Sensor.3.3V, DIP.9, DIP.10, DIP.11, DIP.12, DIP.13, DIP.14, DIP.15, DIP.16, Soil_Hygrometer.VCC, Phototransistor.C, S1.1, S2.1, S3.1
  N20: R2.Pin_1, LED.red_anode
  N21: R3.Pin_1, LED.blue_anode
  N22: R4.Pin_1, LED.green_anode

custom parts:
  DFRobot Capacitive Soil Moisture Sensor V1.0: DFRobot Capacitive Soil Moisture Sensor V1.0 This product measures soil moisture levels by capacitive sensing, rather than resistive sensing like other types of moisture sensor. It is made of a corrosion resistant material giving it a long service life. Insert it into soil and impress your friends with the real-time soil moisture data! The product includes an on-board voltage regulator which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
